// Logisim project s-mips.circ as structural Verilog: 15 circuits, main circuit S-MIPS Board
module S_MIPS_Board (
  input  DESHABILITAR_DISPATCHER,
  output halt
);

  wire button_1_out, CLK, CS, d_ff_1_q, LCLR, LoadRAM, LoadRAMOn, LW, R_R_W, R_W, ram_dispatcher_1_finished,
       RCS, Reset_out, RST, TTY_EN;
  wire [2:0] KDB;
  wire [3:0] LMask, Mask, ram_1_read_time, ram_1_write_time, RMask;
  wire [6:0] KDB_DATA, TTY_DATA;
  wire [15:0] Addr, LAddr, RAddr;
  wire [31:0] I0, I1, I2, I3, LData, ram_1_data_out_0, ram_1_data_out_1, ram_1_data_out_2, ram_1_data_out_3,
       RI0, RI1, RI2, RI3;

  TTY #(.rows(25), .cols(80)) tty_1 (.data(TTY_DATA), .clk(CLK), .we(TTY_EN), .clr(RST));
  not not_1 (LoadRAMOn, ram_dispatcher_1_finished);
  RAM_Dispatcher ram_dispatcher_1 (
    .WriteTime(ram_1_write_time), .Clock(CLK), .Data(LData), .Address(LAddr), .Mask(LMask),
    .Finished(ram_dispatcher_1_finished), .Write(LW), .CLR(LCLR));
  Keyboard #(.buflen(64)) keyboard_1 (.clk(CLK), .re(KDB[0]), .avail(KDB[2]), .data(KDB_DATA));  // open: clr
  RAM ram_1 (
    .Address(RAddr), .Data_Out_0(ram_1_data_out_0), .Data_Out_1(ram_1_data_out_1),
    .Data_Out_2(ram_1_data_out_2), .Data_Out_3(ram_1_data_out_3), .Data_In_0(RI0), .Data_In_1(RI1),
    .Data_In_2(RI2), .Data_In_3(RI3), .Mask(RMask), .nRead_Write(R_R_W), .Chip_Select(RCS),
    .Read_Time(ram_1_read_time), .Reset(button_1_out), .Write_Time(ram_1_write_time));
  Button button_1 (.out(button_1_out));
  D_Flip_Flop d_ff_1 (.clk(CLK), .D(1'b1), .Q(d_ff_1_q), .reset(Reset_out));  // open: Qn, preset, en
  Button Reset (.out(Reset_out));
  S_MIPS s_mips_1 (
    .Kbd_Enable(KDB[0]), .Address(Addr), .Kbd_Clear(KDB[1]), .Kbd_Available(KDB[2]), .RAM_In_0(I0),
    .Kbd_ASCII_Data(KDB_DATA), .RAM_In_1(I1), .TTY_Enable(TTY_EN), .RAM_In_2(I2), .RAM_In_3(I3),
    .TTY_ASCII_Data(TTY_DATA), .Reset(RST), .RAM_Out_0(ram_1_data_out_0), .Clock(CLK),
    .RAM_Out_1(ram_1_data_out_1), .Stop(halt), .RAM_Out_2(ram_1_data_out_2), .RAM_Out_3(ram_1_data_out_3),
    .Mask(Mask), .Read_Time(ram_1_read_time), .Write_Time(ram_1_write_time), .nRead_Write(R_W),
    .Chip_Select(CS));  // open: in_9, in_10, in_11, in_12, Output, Output_2, Output_3
  D_Flip_Flop d_ff_2 (.clk(CLK), .D(d_ff_1_q), .Qn(LCLR), .reset(Reset_out));  // open: Q, preset, en
  or or_1 (RST, LCLR, LoadRAM);
  Clock clock_1 (.out(CLK));
  Multiplexer #(.width(32), .enable("false")) multiplexer_1 (.in0(I0), .in1(LData), .out(RI0), .sel(LoadRAM));
  Multiplexer #(.width(32), .enable("false")) multiplexer_2 (.in0(I1), .in1(LData), .out(RI1), .sel(LoadRAM));
  Multiplexer #(.width(32), .enable("false")) multiplexer_3 (.in0(I2), .in1(LData), .out(RI2), .sel(LoadRAM));
  Multiplexer #(.width(32), .enable("false")) multiplexer_4 (.in0(I3), .in1(LData), .out(RI3), .sel(LoadRAM));
  and and_1 (LoadRAM, ~DESHABILITAR_DISPATCHER, LoadRAMOn);  // AND_Gate
  Multiplexer #(.width(16), .enable("false")) multiplexer_5 (.in0(Addr), .in1(LAddr), .out(RAddr), .sel(LoadRAM));
  Multiplexer #(.width(4), .enable("false")) multiplexer_6 (.in0(Mask), .in1(LMask), .out(RMask), .sel(LoadRAM));
  Multiplexer #(.enable("false")) multiplexer_7 (.in0(CS), .in1(LW), .out(RCS), .sel(LoadRAM));
  Multiplexer #(.enable("false")) multiplexer_8 (.in0(R_W), .in1(LW), .out(R_R_W), .sel(LoadRAM));

  // Notes on the sheet:
  //   NO MODIFICAR
  //   Keyboard
endmodule

module RAM (
  input  [15:0] Address,
  input  [31:0] Data_In_0,
  input  [31:0] Data_In_1,
  input  [31:0] Data_In_2,
  input  [31:0] Data_In_3,
  input  [3:0] Mask,
  input  nRead_Write,
  input  Chip_Select,
  input  Reset,
  output [31:0] Data_Out_0,
  output [31:0] Data_Out_1,
  output [31:0] Data_Out_2,
  output [31:0] Data_Out_3,
  output [3:0] Read_Time,
  output [3:0] Write_Time
);

  wire and_2_out, and_3_out, and_4_out, and_5_out, and_6_out, and_7_out, and_8_out, and_9_out, Changed, CLK,
       comparator_2_eq, comparator_3_eq, comparator_4_eq, comparator_5_eq, comparator_6_eq, Count,
       demultiplexer_3_out0, Idle, Idle_q, Load, Load0, Load1, nand_1_out, or_1_out, or_2_out, or_3_out,
       or_4_out, or_5_out, or_6_out, or_7_out, or_8_out, or_9_out, or_10_out, Proc_q, Update_Mem, Zero_Time;
  wire [3:0] counter_1_q, multiplexer_1_out, subtractor_1_out;
  wire [31:0] register_1_q, register_2_q, register_3_q, register_4_q, register_5_q;

  // Probe on 4'b0011
  // Probe on 4'b0010
  Multiplexer #(.width(4), .enable("false")) multiplexer_1 (
    .in0(4'b0011), .in1(4'b0010), .out(multiplexer_1_out), .sel(nRead_Write));
  or or_1 (or_1_out, Idle, Update_Mem);
  or or_2 (or_2_out, ~Chip_Select, Reset);  // OR_Gate
  Subtractor #(.width(4)) subtractor_1 (.a(multiplexer_1_out), .b(4'b0010), .out(subtractor_1_out));  // open: bin, bout
  D_Flip_Flop u_Idle (.clk(CLK), .D(or_1_out), .Q(Idle_q), .preset(or_2_out));  // open: Qn, en, reset
  Demultiplexer #(.enable("false")) demultiplexer_1 (.out0(Idle), .out1(Load0), .in(Idle_q), .sel(Changed));
  // Probe on counter_1_q
  Counter #(.width(4), .max('hf)) counter_1 (
    .load(Load), .D(subtractor_1_out), .count(Count), .Q(counter_1_q), .clk(CLK), .clr(or_3_out));  // open: carry
  or or_3 (or_3_out, ~Chip_Select, Reset);  // OR_Gate
  Comparator #(.width(4), .mode("unsigned")) comparator_1 (
    .a(4'b0000), .b(counter_1_q), .eq(Zero_Time));  // open: gt, lt
  or or_4 (or_4_out, Count, Load0, Load1);
  Register #(.width(32)) register_1 (.D(Data_In_0), .en(Chip_Select), .Q(register_1_q), .clk(CLK), .clr(or_5_out));
  or or_5 (or_5_out, ~Chip_Select, Reset);  // OR_Gate
  Register #(.width(32)) register_2 (.D(Data_In_1), .en(Chip_Select), .Q(register_2_q), .clk(CLK), .clr(or_6_out));
  or or_6 (or_6_out, ~Chip_Select, Reset);  // OR_Gate
  Register #(.width(32)) register_3 (.D(Data_In_2), .en(Chip_Select), .Q(register_3_q), .clk(CLK), .clr(or_7_out));
  or or_7 (or_7_out, ~Chip_Select, Reset);  // OR_Gate
  Register #(.width(32)) register_4 (.D(Data_In_3), .en(Chip_Select), .Q(register_4_q), .clk(CLK), .clr(or_8_out));
  or or_8 (or_8_out, ~Chip_Select, Reset);  // OR_Gate
  Register #(.width(32)) register_5 (
    .D({{11{1'b1}}, nRead_Write, Mask, Address}), .en(Chip_Select), .Q(register_5_q), .clk(CLK),
    .clr(or_9_out));
  or or_9 (or_9_out, ~Chip_Select, Reset);  // OR_Gate
  D_Flip_Flop Proc (.clk(CLK), .D(or_4_out), .Q(Proc_q), .reset(or_10_out));  // open: Qn, preset, en
  or or_10 (or_10_out, ~Chip_Select, Reset);  // OR_Gate
  Demultiplexer #(.enable("false")) demultiplexer_2 (
    .out0(Count), .out1(Update_Mem), .in(demultiplexer_3_out0), .sel(Zero_Time));
  Demultiplexer #(.enable("false")) demultiplexer_3 (
    .out0(demultiplexer_3_out0), .out1(Load1), .in(Proc_q), .sel(Changed));
  Clock clock_1 (.out(CLK));
  Comparator #(.width(32)) comparator_2 (.a(register_1_q), .b(Data_In_0), .eq(comparator_2_eq));  // open: gt, lt
  Comparator #(.width(32)) comparator_3 (.a(register_2_q), .b(Data_In_1), .eq(comparator_3_eq));  // open: gt, lt
  Comparator #(.width(32)) comparator_4 (.a(register_3_q), .b(Data_In_2), .eq(comparator_4_eq));  // open: gt, lt
  Comparator #(.width(32)) comparator_5 (.a(register_4_q), .b(Data_In_3), .eq(comparator_5_eq));  // open: gt, lt
  Comparator #(.width(32)) comparator_6 (
    .a(register_5_q), .b({{11{1'b1}}, nRead_Write, Mask, Address}), .eq(comparator_6_eq));  // open: gt, lt
  nand nand_1 (nand_1_out, comparator_6_eq, comparator_2_eq, comparator_3_eq, comparator_4_eq, comparator_5_eq);
  and and_1 (Changed, nand_1_out, Chip_Select);
  or or_11 (Load, Count, Load1, Load0);
  and and_2 (and_2_out, Mask[0], Update_Mem, nRead_Write);
  and and_3 (and_3_out, Mask[1], Update_Mem, nRead_Write);
  and and_4 (and_4_out, Mask[2], Update_Mem, nRead_Write);
  and and_5 (and_5_out, Mask[3], Update_Mem, nRead_Write);
  RAM_part #(.addrWidth(16), .dataWidth(32), .bus("separate")) ram_1 (
    .addr(Address), .din(Data_In_0), .data(Data_Out_0), .str(and_2_out), .sel(Chip_Select), .clk(CLK),
    .ld(and_6_out), .clr(Reset));
  and and_6 (and_6_out, ~nRead_Write, Idle);  // AND_Gate
  RAM_part #(.addrWidth(16), .dataWidth(32), .bus("separate")) ram_2 (
    .addr(Address), .din(Data_In_1), .data(Data_Out_1), .str(and_3_out), .sel(Chip_Select), .clk(CLK),
    .ld(and_7_out), .clr(Reset));
  and and_7 (and_7_out, ~nRead_Write, Idle);  // AND_Gate
  RAM_part #(.addrWidth(16), .dataWidth(32), .bus("separate")) ram_3 (
    .addr(Address), .din(Data_In_2), .data(Data_Out_2), .str(and_4_out), .sel(Chip_Select), .clk(CLK),
    .ld(and_8_out), .clr(Reset));
  and and_8 (and_8_out, ~nRead_Write, Idle);  // AND_Gate
  RAM_part #(.addrWidth(16), .dataWidth(32), .bus("separate")) ram_4 (
    .addr(Address), .din(Data_In_3), .data(Data_Out_3), .str(and_5_out), .sel(Chip_Select), .clk(CLK),
    .ld(and_9_out), .clr(Reset));
  and and_9 (and_9_out, ~nRead_Write, Idle);  // AND_Gate

  assign Read_Time = 4'b0011;
  assign Write_Time = 4'b0010;

  // Other names for the same wires on the sheet: M0 = Mask[0]; M1 = Mask[1]; M2 = Mask[2]; M3 = Mask[3];
  //   RW = nRead_Write; CLR = Reset; CS = Chip_Select; Load2 = Count

  // Notes on the sheet:
  //   NO MODIFICAR
  //   excepto quizás los valores RT y WT
  //   BANK0
  //   BANK1
  //   BANK2
  //   BANK3
endmodule

module S_MIPS (
  input  Kbd_Available,
  input  [6:0] Kbd_ASCII_Data,
  input  [31:0] RAM_Out_0,
  input  [31:0] RAM_Out_1,
  input  Reset,
  input  [31:0] RAM_Out_2,
  input  Clock,
  input  [31:0] RAM_Out_3,
  input  [31:0] in_9,
  input  in_10,
  input  in_11,
  input  in_12,
  input  [3:0] Read_Time,
  input  [3:0] Write_Time,
  output Kbd_Enable,
  output [15:0] Address,
  output Kbd_Clear,
  output TTY_Enable,
  output [6:0] TTY_ASCII_Data,
  output Stop,
  output [31:0] RAM_In_0,
  output [31:0] RAM_In_1,
  output [31:0] Output,
  output [31:0] RAM_In_2,
  output Output_2,
  output Output_3,
  output [31:0] RAM_In_3,
  output [3:0] Mask,
  output nRead_Write,
  output Chip_Select
);

  wire clock_1_out;

  Clock clock_1 (.out(clock_1_out));
  RAM_Manager ram_manager_1 (
    .RAM_OUT_0(RAM_Out_0), .RAM_OUT_1(RAM_Out_1), .RAM_OUT_2(RAM_Out_2), .RAM_OUT_3(RAM_Out_3),
    .DATA_PATH_ADDRESS(in_9), .GET_INSTRUCTION(in_10), .GET_DATA(in_11), .WRITE_DATA(in_12),
    .READ_TIME(Read_Time), .WRITE_TIME(Write_Time), .CLOCK(clock_1_out), .RESET(Reset), .DATA_OUT(Output),
    .RAM_ADDRESS(Address), .MASK(Mask), .CHIP_SELECT(Chip_Select), .nR_W(Output_2), .DONE_WRITING(Output_3),
    .DONE_DATA(nRead_Write));  // open: DONE_INSTRUCTION
  // AND_Gate and_1 is placed but not wired

  // Other names for the same wires on the sheet: CLK = Clock; CLR = Reset; CS = Chip_Select;
  //   KBD_AVAIL = Kbd_Available; KBD_CLR = Kbd_Clear; KBD_DATA[6:0] = Kbd_ASCII_Data; RAM_A[15:0] = Address;
  //   RAM_INPUT_0[31:0] = RAM_In_0; RAM_INPUT_1[31:0] = RAM_In_1; RAM_INPUT_2[31:0] = RAM_In_2;
  //   RAM_INPUT_3[31:0] = RAM_In_3; RAM_MASK[3:0] = Mask; RAM_OUTPUT_0[31:0] = RAM_Out_0;
  //   RAM_OUTPUT_1[31:0] = RAM_Out_1; RAM_OUTPUT_2[31:0] = RAM_Out_2; RAM_OUTPUT_3[31:0] = RAM_Out_3;
  //   RW = nRead_Write; TTY_DATA[6:0] = TTY_ASCII_Data

  // Notes on the sheet:
  //   RAM ADDRESS
  //   DATA FROM RAM
  //   DATA TO RAM
  //   DATA WRITE MASK
  //   RAM TIMING
  //   RAM CONTROL
  //   KEYBOARD
  //   TTY
  //   SEQUENCING
endmodule

module RAM_Dispatcher (
  input  [3:0] WriteTime,
  input  Clock,
  input  CLR,
  output [31:0] Data,
  output [15:0] Address,
  output [3:0] Mask,
  output Finished,
  output Write
);

  wire demultiplexer_2_out1, demultiplexer_3_out1, End, IDLE_q, IncAddr, Load, or_1_out, or_2_out, While_q,
       WriteEnd;
  wire [3:0] counter_1_q;
  wire [31:0] CurrentAddress_q;

  Counter #(.width(32), .max('hffffffff)) CurrentAddress (
    .count(IncAddr), .Q({CurrentAddress_q[31:18], Address, CurrentAddress_q[1:0]}), .clk(Clock), .clr(CLR));  // open: load, D, carry
  or or_1 (or_1_out, IncAddr, demultiplexer_3_out1, Finished);
  D_Flip_Flop IDLE (.clk(Clock), .D(or_1_out), .Q(IDLE_q), .preset(CLR));  // open: Qn, en, reset
  Demultiplexer #(.enable("false")) demultiplexer_1 (.out0(Load), .out1(Finished), .in(IDLE_q), .sel(End));
  D_Flip_Flop While (.clk(Clock), .D(or_2_out), .Q(While_q), .reset(CLR));  // open: Qn, preset, en
  or or_2 (or_2_out, Write, Load);
  RAM_part #(.addrWidth(18), .dataWidth(32)) ram_1 (
    .addr({Address, CurrentAddress_q[1:0]}), .data(Data), .clk(Clock));  // open: sel, ld, clr
  Demultiplexer #(.enable("false")) demultiplexer_2 (
    .out0(Write), .out1(demultiplexer_2_out1), .in(While_q), .sel(WriteEnd));
  Decoder #(.select(2)) decoder_1 (
    .out0(Mask[0]), .out1(Mask[1]), .out2(Mask[2]), .out3(Mask[3]), .sel(CurrentAddress_q[1:0]));  // open: en
  Demultiplexer #(.enable("false")) demultiplexer_3 (
    .out0(IncAddr), .out1(demultiplexer_3_out1), .in(demultiplexer_2_out1), .sel(End));
  Counter #(.width(4), .max('hf)) counter_1 (
    .load(Load), .D(WriteTime), .count(Write), .Q(counter_1_q), .clk(Clock));  // open: carry, clr
  Comparator #(.width(32)) comparator_1 (.a(Data), .b({32{1'b1}}), .eq(End));  // open: gt, lt
  Comparator #(.width(4)) comparator_2 (.a(4'b0000), .b(counter_1_q), .eq(WriteEnd));  // open: gt, lt

  // Other names for the same wires on the sheet: CLK = Clock; Count = Write; WT[3:0] = WriteTime
endmodule

module RAM_Manager (
  input  [31:0] RAM_OUT_0,
  input  [31:0] RAM_OUT_1,
  input  [31:0] RAM_OUT_2,
  input  [31:0] RAM_OUT_3,
  input  [31:0] DATA_PATH_ADDRESS,
  input  GET_INSTRUCTION,
  input  GET_DATA,
  input  WRITE_DATA,
  input  [3:0] READ_TIME,
  input  [3:0] WRITE_TIME,
  input  CLOCK,
  input  RESET,
  output [31:0] DATA_OUT,
  output [15:0] RAM_ADDRESS,
  output [3:0] MASK,
  output CHIP_SELECT,
  output nR_W,
  output DONE_WRITING,
  output DONE_DATA,
  output DONE_INSTRUCTION
);

  wire d_ff_2_q, d_ff_3_q, d_ff_4_q, d_ff_5_q, demultiplexer_2_out0, demultiplexer_2_out1,
       demultiplexer_3_out0, demultiplexer_3_out1, DONE_READING, nDATA_INSTRUCTION, or_2_out, READING,
       READING_TIME_OUT, RESTORE_READING_TYPE, START_READING, START_WRITING, WRITING_TIME_OUT;
  wire [31:0] n4_byte_flipper_1_out, n4_byte_flipper_2_out, n4_byte_flipper_3_out, n4_byte_flipper_4_out,
       RAM_STORED_0, RAM_STORED_1, RAM_STORED_2, RAM_STORED_3;

  or or_1 (READING, GET_DATA, GET_INSTRUCTION);
  or or_2 (or_2_out, GET_INSTRUCTION, GET_DATA);
  D_Flip_Flop #(.trigger("falling")) d_ff_1 (
    .clk(CLOCK), .D(GET_INSTRUCTION), .Q(nDATA_INSTRUCTION), .en(READING), .reset(RESTORE_READING_TYPE));  // open: Qn, preset
  D_Flip_Flop #(.trigger("falling")) d_ff_2 (
    .clk(CLOCK), .D(or_2_out), .Q(d_ff_2_q), .reset(RESET));  // open: Qn, preset, en
  D_Flip_Flop #(.trigger("falling")) d_ff_3 (
    .clk(CLOCK), .D(WRITE_DATA), .Q(d_ff_3_q), .reset(RESET));  // open: Qn, preset, en
  _4_Byte_Flipper u_4_byte_flipper_1 (.IN(RAM_OUT_0), .OUT(n4_byte_flipper_1_out));
  _4_Byte_Flipper u_4_byte_flipper_2 (.IN(RAM_OUT_1), .OUT(n4_byte_flipper_2_out));
  _4_Byte_Flipper u_4_byte_flipper_3 (.IN(RAM_OUT_2), .OUT(n4_byte_flipper_3_out));
  _4_Byte_Flipper u_4_byte_flipper_4 (.IN(RAM_OUT_3), .OUT(n4_byte_flipper_4_out));
  or or_3 (START_READING, demultiplexer_2_out0, d_ff_2_q);
  or or_4 (START_WRITING, demultiplexer_3_out0, d_ff_3_q);
  and and_1 (nR_W, ~READING, WRITE_DATA);  // AND_Gate
  Demultiplexer #(.select(2)) demultiplexer_1 (
    .out0(MASK[0]), .out1(MASK[1]), .out2(MASK[2]), .out3(MASK[3]), .in(1'b1), .sel(DATA_PATH_ADDRESS[3:2]));  // open: en
  D_Flip_Flop #(.trigger("falling")) d_ff_4 (
    .clk(CLOCK), .D(START_READING), .Q(d_ff_4_q), .reset(DONE_READING));  // open: Qn, preset, en
  Register #(.width(32)) register_1 (
    .D(n4_byte_flipper_1_out), .en(DONE_READING), .Q(RAM_STORED_0), .clk(CLOCK), .clr(RESET));
  Register #(.width(32)) register_2 (
    .D(n4_byte_flipper_2_out), .en(DONE_READING), .Q(RAM_STORED_1), .clk(CLOCK), .clr(RESET));
  Register #(.width(32)) register_3 (
    .D(n4_byte_flipper_3_out), .en(DONE_READING), .Q(RAM_STORED_2), .clk(CLOCK), .clr(RESET));
  Register #(.width(32)) register_4 (
    .D(n4_byte_flipper_4_out), .en(DONE_READING), .Q(RAM_STORED_3), .clk(CLOCK), .clr(RESET));
  Demultiplexer demultiplexer_2 (
    .out0(demultiplexer_2_out0), .out1(demultiplexer_2_out1), .in(d_ff_4_q), .sel(READING_TIME_OUT));  // open: en
  Demultiplexer demultiplexer_3 (
    .out0(demultiplexer_3_out0), .out1(demultiplexer_3_out1), .in(d_ff_5_q), .sel(WRITING_TIME_OUT));  // open: en
  D_Flip_Flop #(.trigger("falling")) d_ff_5 (
    .clk(CLOCK), .D(START_WRITING), .Q(d_ff_5_q), .reset(DONE_WRITING));  // open: Qn, preset, en
  and and_2 (DONE_DATA, ~nDATA_INSTRUCTION, DONE_READING);  // AND_Gate
  and and_3 (DONE_INSTRUCTION, nDATA_INSTRUCTION, DONE_READING);
  D_Flip_Flop #(.trigger("falling")) d_ff_6 (
    .clk(CLOCK), .D(demultiplexer_2_out1), .Q(DONE_READING));  // open: Qn, preset, en, reset
  D_Flip_Flop #(.trigger("falling")) d_ff_7 (
    .clk(CLOCK), .D(demultiplexer_3_out1), .Q(DONE_WRITING));  // open: Qn, preset, en, reset
  D_Flip_Flop #(.trigger("falling")) d_ff_8 (
    .clk(CLOCK), .D(DONE_READING), .Q(RESTORE_READING_TYPE));  // open: Qn, preset, en, reset
  Multiplexer #(.select(2), .width(32)) multiplexer_1 (
    .in0(RAM_STORED_0), .in1(RAM_STORED_1), .in2(RAM_STORED_2), .in3(RAM_STORED_3), .out(DATA_OUT),
    .sel(DATA_PATH_ADDRESS[3:2]));  // open: en
  Timer timer_1 (
    .START(START_READING), .TIME(READ_TIME), .CLOCK(CLOCK), .RESET(DONE_READING), .TIME_OUT(READING_TIME_OUT));
  Timer timer_2 (
    .START(START_WRITING), .TIME(WRITE_TIME), .CLOCK(CLOCK), .RESET(DONE_WRITING), .TIME_OUT(WRITING_TIME_OUT));
  or or_5 (CHIP_SELECT, START_WRITING, START_READING);
  // AND_Gate and_4 is placed but not wired

  assign RAM_ADDRESS = DATA_PATH_ADDRESS[19:4];

  // Other names for the same wires on the sheet: MASK_SELECTOR[1:0] = DATA_PATH_ADDRESS[3:2];
  //   STORE_RAM_DATA = DONE_READING

  // Notes on the sheet:
  //   INPUTS
  //   OUTPUTS
endmodule

module Data_Path (
  input  [31:0] INSTRUCTION,
  input  [31:0] DATA_FROM_RAM,
  input  ENABLE_REGISTER_FILE,
  input  ENABLE_PC,
  input  NEW_INSTRUCTION,
  input  CLOCK,
  input  RESET,
  output [31:0] DATA_TO_RAM,
  output [31:0] RAM_ADDRESS,
  output [31:0] PC,
  output [6:0] TTY_DATA,
  output TTY_ENABLE,
  output HALT
);

  wire ADD, ADDI, ALU_SIGN, AND, and_1_out, and_2_out, and_3_out, and_4_out, and_5_out, ANDI, BEQ, BGTZ,
       BLEZ, BLTZ, BNE, BRANCH, DIV, DIVU, ENABLE_LOW_HIGH, ENABLE_STACK_POINTER, IMMEDIATE_TO_ALU, J, JR,
       JUMP, KBD, LW, MFHI, MFLO, MULT, MULU, NOP, NOR, OR, ORI, POP, PUSH, RS___0, RS___0_t, RS____0,
       RS____0_t, RS____RT, SLT, SLTI, SLTIU, SLTU, STACK_INSTRUCTION, STORE_IN_RT, STORING_FROM_RAM, SUB,
       SW, XOR, XORI, ZERO_EXTENDED_IMMEDIATE;
  wire [2:0] RF_DATA_SELECTOR;
  wire [3:0] ALU_SELECTOR;
  wire [4:0] RD_SELECTOR, RF_WRITE_SELECTOR, RS_SELECTOR, RT_SELECTOR;
  wire [15:0] IMMEDIATE_VALUE;
  wire [27:2] J_ADDRESS_EXTENDED;
  wire [31:0] adder_3_out, ALU_IN_B, ALU_OUT, bit_extender_1_out, bit_extender_2_out, EXTENDED_IMMEDIATE,
       IN_HIGH, IN_LOW, IN_PC, multiplexer_4_out, multiplexer_5_out, OUT_HIGH, OUT_LOW, PC___4,
       PC___4___SHIFTED_OFFSET, RANDOM, RF_DATA_IN, RT_VALUE, SHIFTED_OFFSET, STACK_POINTER_IN,
       STACK_POINTER_OUT, subtractor_1_out;
  wire [31:7] RS_VALUE;

  or or_1 (STORING_FROM_RAM, POP, LW);
  or or_2 (STACK_INSTRUCTION, POP, PUSH);
  Random #(.width(32)) random_1 (.clk(CLOCK), .next(1'b1), .out(RANDOM), .clr(RESET));
  Adder #(.width(32)) adder_1 (.a(PC), .b(32'h4), .out(PC___4));  // open: cin, cout
  Shifter #(.width(32)) shifter_1 (.in(EXTENDED_IMMEDIATE), .\dist (5'b00010), .out(SHIFTED_OFFSET));
  Adder #(.width(32)) adder_2 (.a(PC___4), .b(SHIFTED_OFFSET), .out(PC___4___SHIFTED_OFFSET));  // open: cin, cout
  Comparator #(.width(32)) comparator_1 (.a({RS_VALUE, TTY_DATA}), .b(RT_VALUE), .eq(RS____RT));  // open: gt, lt
  Comparator #(.width(32)) comparator_2 (
    .a({RS_VALUE, TTY_DATA}), .b({32{1'b0}}), .gt(RS___0_t), .eq(RS____0_t), .lt(RS___0));
  or or_3 (RS____0, RS____0_t, RS___0);
  and and_1 (and_1_out, BEQ, RS____RT);
  and and_2 (and_2_out, BNE, ~RS____RT);  // AND_Gate
  and and_3 (and_3_out, BLEZ, RS____0);
  and and_4 (and_4_out, BGTZ, RS___0_t);
  and and_5 (and_5_out, BLTZ, RS___0);
  or or_4 (JUMP, J, JR);
  or or_5 (STORE_IN_RT, ADDI, ANDI, ORI, XORI, SLTI, SLTIU, LW);
  or or_6 (BRANCH, and_1_out, and_2_out, and_3_out, and_4_out, and_5_out);
  Multiplexer #(.width(5)) multiplexer_1 (
    .in0(RD_SELECTOR), .in1(RT_SELECTOR), .out(RF_WRITE_SELECTOR), .sel(STORE_IN_RT));  // open: en
  Multiplexer #(.select(3), .width(32)) multiplexer_2 (
    .in0(ALU_OUT), .in1(DATA_FROM_RAM), .in2(OUT_LOW), .in3(OUT_HIGH), .in4(RANDOM), .out(RF_DATA_IN),
    .sel(RF_DATA_SELECTOR));  // open: in5, in6, in7, en
  and and_6 (ENABLE_STACK_POINTER, NEW_INSTRUCTION, STACK_INSTRUCTION);
  Adder #(.width(32)) adder_3 (.a(STACK_POINTER_OUT), .b(32'h4), .out(adder_3_out));  // open: cin, cout
  Subtractor #(.width(32)) subtractor_1 (.a(STACK_POINTER_OUT), .b(32'h4), .out(subtractor_1_out));  // open: bin, bout
  Multiplexer #(.width(32)) multiplexer_3 (
    .in0(adder_3_out), .in1(subtractor_1_out), .out(STACK_POINTER_IN), .sel(PUSH));  // open: en
  Multiplexer #(.width(32)) multiplexer_4 (
    .in0(PC___4), .in1(PC___4___SHIFTED_OFFSET), .out(multiplexer_4_out), .sel(BRANCH));  // open: en
  Multiplexer #(.width(32)) multiplexer_5 (
    .in0({RS_VALUE, TTY_DATA}), .in1({PC[31:28], J_ADDRESS_EXTENDED, 2'b00}), .out(multiplexer_5_out), .sel(J));  // open: en
  Instruction_Decoder instruction_decoder_1 (
    .INSTRUCTION(INSTRUCTION), .NOP(NOP), .ADD(ADD), .SUB(SUB), .MULT(MULT), .MULU(MULU), .DIV(DIV),
    .DIVU(DIVU), .SLT(SLT), .SLTU(SLTU), .AND(AND), .OR(OR), .NOR(NOR), .XOR(XOR), .JR(JR), .MFHI(MFHI),
    .MFLO(MFLO), .POP(POP), .PUSH(PUSH), .HALT(HALT), .TTY(TTY_ENABLE), .RND(RF_DATA_SELECTOR[2]), .KBD(KBD),
    .ADDI(ADDI), .SLTI(SLTI), .SLTIU(SLTIU), .ANDI(ANDI), .ORI(ORI), .XORI(XORI), .LW(LW), .SW(SW),
    .BEQ(BEQ), .BNE(BNE), .BLEZ(BLEZ), .BGTZ(BGTZ), .BLTZ(BLTZ), .J(J), .IMMEDIATE_VALUE(IMMEDIATE_VALUE),
    .JUMP_ADDRESS(J_ADDRESS_EXTENDED), .RD_SELECTOR(RD_SELECTOR), .RT_SELECTOR(RT_SELECTOR),
    .RS_SELECTOR(RS_SELECTOR));
  Multiplexer #(.width(32)) multiplexer_6 (
    .in0(multiplexer_4_out), .in1(multiplexer_5_out), .out(IN_PC), .sel(JUMP));  // open: en
  PC_Register pc_register_1 (.IN_PC(IN_PC), .ENABLE_PC(ENABLE_PC), .CLOCK(CLOCK), .RESET(RESET), .OUT_PC(PC));
  or or_7 (RF_DATA_SELECTOR[0], STORING_FROM_RAM, MFHI);
  or or_8 (RF_DATA_SELECTOR[1], MFLO, MFHI);
  Multiplexer #(.width(32)) multiplexer_7 (
    .in0(ALU_OUT), .in1(STACK_POINTER_OUT), .out(RAM_ADDRESS), .sel(STACK_INSTRUCTION));  // open: en
  Multiplexer #(.width(32)) multiplexer_8 (
    .in0(RT_VALUE), .in1({RS_VALUE, TTY_DATA}), .out(DATA_TO_RAM), .sel(STACK_INSTRUCTION));  // open: en
  Register_File register_file_1 (
    .DATA_IN(RF_DATA_IN), .STACK_POINTER_IN(STACK_POINTER_IN), .SELECT_A(RS_SELECTOR),
    .SELECT_B(RT_SELECTOR), .SELECT_TO_WRITE(RF_WRITE_SELECTOR), .ENABLE_WRITE(ENABLE_REGISTER_FILE),
    .ENABLE_STACK_POINTER(ENABLE_STACK_POINTER), .CLOCK(CLOCK), .RESET(RESET), .OUT_A({RS_VALUE, TTY_DATA}),
    .OUT_B(RT_VALUE), .STACK_POINTER_OUT(STACK_POINTER_OUT));
  or or_9 (ZERO_EXTENDED_IMMEDIATE, ANDI, ORI, XORI);
  assign bit_extender_1_out = {{16{IMMEDIATE_VALUE[15]}}, IMMEDIATE_VALUE};  // Bit_Extender bit_extender_1
  assign bit_extender_2_out = {{16{1'b0}}, IMMEDIATE_VALUE};  // Bit_Extender bit_extender_2
  or or_10 (IMMEDIATE_TO_ALU, STORE_IN_RT, SW);
  Multiplexer #(.width(32)) multiplexer_9 (
    .in0(bit_extender_1_out), .in1(bit_extender_2_out), .out(EXTENDED_IMMEDIATE),
    .sel(ZERO_EXTENDED_IMMEDIATE));  // open: en
  Multiplexer #(.width(32)) multiplexer_10 (
    .in0(RT_VALUE), .in1(EXTENDED_IMMEDIATE), .out(ALU_IN_B), .sel(IMMEDIATE_TO_ALU));  // open: en
  ALU alu_1 (
    .IN_A({RS_VALUE, TTY_DATA}), .IN_B(ALU_IN_B), .SIGN(ALU_SIGN), .OPERATION_SELECTOR(ALU_SELECTOR),
    .OUT(ALU_OUT), .LOW(IN_LOW), .HIGH(IN_HIGH));
  ALU_Manager alu_manager_1 (
    .SUB(SUB), .NOR(NOR), .MULT(MULT), .MULU(MULU), .DIV(DIV), .DIVU(DIVU), .AND(AND), .ANDI(ANDI), .OR(OR),
    .ORI(ORI), .XOR(XOR), .XORI(XORI), .SLT(SLT), .SLTU(SLTU), .SLTI(SLTI), .SLTIU(SLTIU),
    .ALU_SELECTOR(ALU_SELECTOR), .ALU_SIGN(ALU_SIGN));
  or or_11 (ENABLE_LOW_HIGH, MULT, MULU, DIV, DIVU);
  Low_High_Registers low_high_registers_1 (
    .IN_LOW(IN_LOW), .IN_HIGH(IN_HIGH), .ENABLE(ENABLE_LOW_HIGH), .CLOCK(CLOCK), .RESET(RESET),
    .OUT_LOW(OUT_LOW), .OUT_HIGH(OUT_HIGH));
  // AND_Gate and_7 is placed but not wired

  // Other names for the same wires on the sheet: ENABLE_RF = ENABLE_REGISTER_FILE;
  //   JUMP_ADDRESS[25:0] = J_ADDRESS_EXTENDED; J_ADDRESS_EXTENDED[31:28] = PC[31:28]; OUT_PC[31:0] = PC;
  //   RND = RF_DATA_SELECTOR[2]; TTY = TTY_ENABLE; RS_VALUE[6:0] = TTY_DATA

  // Notes on the sheet:
  //   INPUTS FROM CONTROL UNIT
  //   INPUTS FROM RAM MANAGER AND INTRUCTION/RAM REGISTERS
  //   MANAGING BRANCHING
  //   MANAGING REGISTER FILE
  //   MANAGING ALU
  //   SPECIAL INSTRUCTION
endmodule

module Instruction_Decoder (
  input  [31:0] INSTRUCTION,
  output NOP,
  output ADD,
  output SUB,
  output MULT,
  output MULU,
  output DIV,
  output DIVU,
  output SLT,
  output SLTU,
  output AND,
  output OR,
  output NOR,
  output XOR,
  output JR,
  output MFHI,
  output MFLO,
  output POP,
  output PUSH,
  output HALT,
  output TTY,
  output RND,
  output KBD,
  output ADDI,
  output SLTI,
  output SLTIU,
  output ANDI,
  output ORI,
  output XORI,
  output LW,
  output SW,
  output BEQ,
  output BNE,
  output BLEZ,
  output BGTZ,
  output BLTZ,
  output J,
  output [15:0] IMMEDIATE_VALUE,
  output [25:0] JUMP_ADDRESS,
  output [4:0] RD_SELECTOR,
  output [4:0] RT_SELECTOR,
  output [4:0] RS_SELECTOR
);

  wire and_2_out, and_3_out, and_4_out, and_5_out, and_6_out, and_7_out, and_8_out, and_9_out, and_10_out,
       and_11_out, and_12_out, and_13_out, and_14_out, and_15_out, and_16_out, and_17_out, and_48_out,
       and_49_out, and_51_out, and_52_out, and_53_out, and_54_out, CLASSICAL_R_INSTRUCTION,
       SPECIAL_R_INSTRUCTION, STACK_R_INSTRUCTION;

  and and_1 (CLASSICAL_R_INSTRUCTION, ~INSTRUCTION[26], ~INSTRUCTION[27], ~INSTRUCTION[28], ~INSTRUCTION[29], ~INSTRUCTION[30], ~INSTRUCTION[31]);  // AND_Gate
  and and_2 (and_2_out, ~INSTRUCTION[0], ~INSTRUCTION[1], ~INSTRUCTION[2], ~INSTRUCTION[3], ~INSTRUCTION[4], ~INSTRUCTION[5]);  // AND_Gate
  and and_3 (and_3_out, ~INSTRUCTION[0], ~INSTRUCTION[1], ~INSTRUCTION[2], ~INSTRUCTION[3], ~INSTRUCTION[4], INSTRUCTION[5]);  // AND_Gate
  and and_4 (and_4_out, ~INSTRUCTION[0], INSTRUCTION[1], ~INSTRUCTION[2], ~INSTRUCTION[3], ~INSTRUCTION[4], INSTRUCTION[5]);  // AND_Gate
  and and_5 (and_5_out, ~INSTRUCTION[0], ~INSTRUCTION[1], ~INSTRUCTION[2], INSTRUCTION[3], INSTRUCTION[4], ~INSTRUCTION[5]);  // AND_Gate
  and and_6 (and_6_out, INSTRUCTION[0], ~INSTRUCTION[1], ~INSTRUCTION[2], INSTRUCTION[3], INSTRUCTION[4], ~INSTRUCTION[5]);  // AND_Gate
  and and_7 (and_7_out, ~INSTRUCTION[0], INSTRUCTION[1], ~INSTRUCTION[2], INSTRUCTION[3], INSTRUCTION[4], ~INSTRUCTION[5]);  // AND_Gate
  and and_8 (and_8_out, INSTRUCTION[0], INSTRUCTION[1], ~INSTRUCTION[2], INSTRUCTION[3], INSTRUCTION[4], ~INSTRUCTION[5]);  // AND_Gate
  and and_9 (and_9_out, ~INSTRUCTION[0], INSTRUCTION[1], ~INSTRUCTION[2], INSTRUCTION[3], ~INSTRUCTION[4], INSTRUCTION[5]);  // AND_Gate
  and and_10 (and_10_out, INSTRUCTION[0], INSTRUCTION[1], ~INSTRUCTION[2], INSTRUCTION[3], ~INSTRUCTION[4], INSTRUCTION[5]);  // AND_Gate
  and and_11 (and_11_out, ~INSTRUCTION[0], ~INSTRUCTION[1], INSTRUCTION[2], ~INSTRUCTION[3], ~INSTRUCTION[4], INSTRUCTION[5]);  // AND_Gate
  and and_12 (and_12_out, INSTRUCTION[0], ~INSTRUCTION[1], INSTRUCTION[2], ~INSTRUCTION[3], ~INSTRUCTION[4], INSTRUCTION[5]);  // AND_Gate
  and and_13 (and_13_out, INSTRUCTION[0], INSTRUCTION[1], INSTRUCTION[2], ~INSTRUCTION[3], ~INSTRUCTION[4], INSTRUCTION[5]);  // AND_Gate
  and and_14 (and_14_out, ~INSTRUCTION[0], ~INSTRUCTION[1], ~INSTRUCTION[2], INSTRUCTION[3], ~INSTRUCTION[4], INSTRUCTION[5]);  // AND_Gate
  and and_15 (and_15_out, ~INSTRUCTION[0], ~INSTRUCTION[1], ~INSTRUCTION[2], INSTRUCTION[3], ~INSTRUCTION[4], ~INSTRUCTION[5]);  // AND_Gate
  and and_16 (and_16_out, ~INSTRUCTION[0], ~INSTRUCTION[1], ~INSTRUCTION[2], ~INSTRUCTION[3], INSTRUCTION[4], ~INSTRUCTION[5]);  // AND_Gate
  and and_17 (and_17_out, ~INSTRUCTION[0], INSTRUCTION[1], ~INSTRUCTION[2], ~INSTRUCTION[3], INSTRUCTION[4], ~INSTRUCTION[5]);  // AND_Gate
  and and_18 (ADDI, ~INSTRUCTION[26], ~INSTRUCTION[27], ~INSTRUCTION[28], INSTRUCTION[29], ~INSTRUCTION[30], ~INSTRUCTION[31]);  // AND_Gate
  and and_19 (SLTI, ~INSTRUCTION[26], INSTRUCTION[27], ~INSTRUCTION[28], INSTRUCTION[29], ~INSTRUCTION[30], ~INSTRUCTION[31]);  // AND_Gate
  and and_20 (SLTIU, INSTRUCTION[26], INSTRUCTION[27], ~INSTRUCTION[28], INSTRUCTION[29], ~INSTRUCTION[30], ~INSTRUCTION[31]);  // AND_Gate
  and and_21 (ANDI, ~INSTRUCTION[26], ~INSTRUCTION[27], INSTRUCTION[28], INSTRUCTION[29], ~INSTRUCTION[30], ~INSTRUCTION[31]);  // AND_Gate
  and and_22 (ORI, INSTRUCTION[26], ~INSTRUCTION[27], INSTRUCTION[28], INSTRUCTION[29], ~INSTRUCTION[30], ~INSTRUCTION[31]);  // AND_Gate
  and and_23 (XORI, ~INSTRUCTION[26], INSTRUCTION[27], INSTRUCTION[28], INSTRUCTION[29], ~INSTRUCTION[30], ~INSTRUCTION[31]);  // AND_Gate
  and and_24 (LW, INSTRUCTION[26], INSTRUCTION[27], ~INSTRUCTION[28], ~INSTRUCTION[29], ~INSTRUCTION[30], INSTRUCTION[31]);  // AND_Gate
  and and_25 (SW, INSTRUCTION[26], INSTRUCTION[27], ~INSTRUCTION[28], INSTRUCTION[29], ~INSTRUCTION[30], INSTRUCTION[31]);  // AND_Gate
  and and_26 (BEQ, ~INSTRUCTION[26], ~INSTRUCTION[27], INSTRUCTION[28], ~INSTRUCTION[29], ~INSTRUCTION[30], ~INSTRUCTION[31]);  // AND_Gate
  and and_27 (BNE, INSTRUCTION[26], ~INSTRUCTION[27], INSTRUCTION[28], ~INSTRUCTION[29], ~INSTRUCTION[30], ~INSTRUCTION[31]);  // AND_Gate
  and and_28 (BLEZ, ~INSTRUCTION[26], INSTRUCTION[27], INSTRUCTION[28], ~INSTRUCTION[29], ~INSTRUCTION[30], ~INSTRUCTION[31]);  // AND_Gate
  and and_29 (BGTZ, INSTRUCTION[26], INSTRUCTION[27], INSTRUCTION[28], ~INSTRUCTION[29], ~INSTRUCTION[30], ~INSTRUCTION[31]);  // AND_Gate
  and and_30 (BLTZ, INSTRUCTION[26], ~INSTRUCTION[27], ~INSTRUCTION[28], ~INSTRUCTION[29], ~INSTRUCTION[30], ~INSTRUCTION[31]);  // AND_Gate
  and and_31 (NOP, CLASSICAL_R_INSTRUCTION, and_2_out);
  and and_32 (ADD, CLASSICAL_R_INSTRUCTION, and_3_out);
  and and_33 (SUB, CLASSICAL_R_INSTRUCTION, and_4_out);
  and and_34 (MULT, CLASSICAL_R_INSTRUCTION, and_5_out);
  and and_35 (MULU, CLASSICAL_R_INSTRUCTION, and_6_out);
  and and_36 (DIV, CLASSICAL_R_INSTRUCTION, and_7_out);
  and and_37 (DIVU, CLASSICAL_R_INSTRUCTION, and_8_out);
  and and_38 (SLT, CLASSICAL_R_INSTRUCTION, and_9_out);
  and and_39 (SLTU, CLASSICAL_R_INSTRUCTION, and_10_out);
  and and_40 (AND, CLASSICAL_R_INSTRUCTION, and_11_out);
  and and_41 (OR, CLASSICAL_R_INSTRUCTION, and_12_out);
  and and_42 (NOR, CLASSICAL_R_INSTRUCTION, and_13_out);
  and and_43 (XOR, CLASSICAL_R_INSTRUCTION, and_14_out);
  and and_44 (JR, CLASSICAL_R_INSTRUCTION, and_15_out);
  and and_45 (MFHI, CLASSICAL_R_INSTRUCTION, and_16_out);
  and and_46 (MFLO, CLASSICAL_R_INSTRUCTION, and_17_out);
  and and_47 (STACK_R_INSTRUCTION, ~INSTRUCTION[26], ~INSTRUCTION[27], ~INSTRUCTION[28], INSTRUCTION[29], INSTRUCTION[30], INSTRUCTION[31]);  // AND_Gate
  and and_48 (and_48_out, ~INSTRUCTION[0], ~INSTRUCTION[1], ~INSTRUCTION[2], ~INSTRUCTION[3], ~INSTRUCTION[4], ~INSTRUCTION[5]);  // AND_Gate
  and and_49 (and_49_out, INSTRUCTION[0], ~INSTRUCTION[1], ~INSTRUCTION[2], ~INSTRUCTION[3], ~INSTRUCTION[4], ~INSTRUCTION[5]);  // AND_Gate
  and and_50 (SPECIAL_R_INSTRUCTION, INSTRUCTION[26], INSTRUCTION[27], INSTRUCTION[28], INSTRUCTION[29], INSTRUCTION[30], INSTRUCTION[31]);
  and and_51 (and_51_out, INSTRUCTION[0], INSTRUCTION[1], INSTRUCTION[2], INSTRUCTION[3], INSTRUCTION[4], INSTRUCTION[5]);
  and and_52 (and_52_out, INSTRUCTION[0], ~INSTRUCTION[1], ~INSTRUCTION[2], ~INSTRUCTION[3], ~INSTRUCTION[4], ~INSTRUCTION[5]);  // AND_Gate
  and and_53 (and_53_out, ~INSTRUCTION[0], INSTRUCTION[1], ~INSTRUCTION[2], ~INSTRUCTION[3], ~INSTRUCTION[4], ~INSTRUCTION[5]);  // AND_Gate
  and and_54 (and_54_out, ~INSTRUCTION[0], ~INSTRUCTION[1], INSTRUCTION[2], ~INSTRUCTION[3], ~INSTRUCTION[4], ~INSTRUCTION[5]);  // AND_Gate
  and and_55 (J, ~INSTRUCTION[26], INSTRUCTION[27], ~INSTRUCTION[28], ~INSTRUCTION[29], ~INSTRUCTION[30], ~INSTRUCTION[31]);  // AND_Gate
  and and_56 (POP, STACK_R_INSTRUCTION, and_48_out);
  and and_57 (PUSH, STACK_R_INSTRUCTION, and_49_out);
  and and_58 (HALT, SPECIAL_R_INSTRUCTION, and_51_out);
  and and_59 (TTY, SPECIAL_R_INSTRUCTION, and_52_out);
  and and_60 (RND, SPECIAL_R_INSTRUCTION, and_53_out);
  and and_61 (KBD, SPECIAL_R_INSTRUCTION, and_54_out);
  // AND_Gate and_62 is placed but not wired

  assign IMMEDIATE_VALUE = INSTRUCTION[15:0];
  assign JUMP_ADDRESS = INSTRUCTION[25:0];
  assign RD_SELECTOR = INSTRUCTION[15:11];
  assign RS_SELECTOR = INSTRUCTION[25:21];
  assign RT_SELECTOR = INSTRUCTION[20:16];

  // Other names for the same wires on the sheet: FUNC[5:0] = INSTRUCTION[5:0]; OP_CODE[5:0] = INSTRUCTION[31:26];
  //   RD[4:0] = INSTRUCTION[15:11]; RS[4:0] = INSTRUCTION[25:21]; RT[4:0] = INSTRUCTION[20:16]

  // Notes on the sheet:
  //   I_INSTRUCTIONS
  //   R_INSTRUCTIONS
  //   J_INSTRUCTION
  //   OUTPUTS
endmodule

module Register_File (
  input  [31:0] DATA_IN,
  input  [31:0] STACK_POINTER_IN,
  input  [4:0] SELECT_A,
  input  [4:0] SELECT_B,
  input  [4:0] SELECT_TO_WRITE,
  input  ENABLE_WRITE,
  input  ENABLE_STACK_POINTER,
  input  CLOCK,
  input  RESET,
  output [31:0] OUT_A,
  output [31:0] OUT_B,
  output [31:0] STACK_POINTER_OUT
);

  wire ENABLE_31, L0, L1, L2, L3, L4, L5, L6, L7, L8, L9, L10, L11, L12, L13, L14, L15, L16, L17, L18, L19,
       L20, L21, L22, L23, L24, L25, L26, L27, L28, L29, L30, L31;
  wire [31:0] DATA_IN_31, OUT0, OUT1, OUT2, OUT3, OUT4, OUT5, OUT6, OUT7, OUT8, OUT9, OUT10, OUT11, OUT12,
       OUT13, OUT14, OUT15, OUT16, OUT17, OUT18, OUT19, OUT20, OUT21, OUT22, OUT23, OUT24, OUT25, OUT26,
       OUT27, OUT28, OUT29, OUT30;

  Multiplexer #(.width(32)) multiplexer_1 (
    .in0(DATA_IN), .in1(STACK_POINTER_IN), .out(DATA_IN_31), .sel(ENABLE_STACK_POINTER));  // open: en
  or or_1 (ENABLE_31, L31, ENABLE_STACK_POINTER);
  Demultiplexer #(.select(5)) demultiplexer_1 (
    .out0(L0), .out1(L1), .out2(L2), .out3(L3), .out4(L4), .out5(L5), .out6(L6), .out7(L7), .out8(L8),
    .out9(L9), .out10(L10), .out11(L11), .out12(L12), .out13(L13), .out14(L14), .out15(L15), .out16(L16),
    .out17(L17), .out18(L18), .out19(L19), .out20(L20), .out21(L21), .out22(L22), .out23(L23), .out24(L24),
    .out25(L25), .out26(L26), .out27(L27), .out28(L28), .out29(L29), .out30(L30), .out31(L31),
    .in(ENABLE_WRITE), .sel(SELECT_TO_WRITE));  // open: en
  Multiplexer #(.select(5), .width(32)) multiplexer_2 (
    .in0(OUT0), .in1(OUT1), .in2(OUT2), .in3(OUT3), .in4(OUT4), .in5(OUT5), .in6(OUT6), .in7(OUT7),
    .in8(OUT8), .in9(OUT9), .in10(OUT10), .in11(OUT11), .in12(OUT12), .in13(OUT13), .in14(OUT14),
    .in15(OUT15), .in16(OUT16), .in17(OUT17), .in18(OUT18), .in19(OUT19), .in20(OUT20), .in21(OUT21),
    .in22(OUT22), .in23(OUT23), .in24(OUT24), .in25(OUT25), .in26(OUT26), .in27(OUT27), .in28(OUT28),
    .in29(OUT29), .in30(OUT30), .in31(STACK_POINTER_OUT), .out(OUT_A), .sel(SELECT_A));  // open: en
  Register #(.width(32)) register_1 (.D({32{1'b0}}), .en(L0), .Q(OUT0), .clk(CLOCK), .clr(RESET));
  Register #(.width(32)) register_2 (.D(DATA_IN), .en(L6), .Q(OUT6), .clk(CLOCK), .clr(RESET));
  Register #(.width(32)) register_3 (.D(DATA_IN), .en(L12), .Q(OUT12), .clk(CLOCK), .clr(RESET));
  Register #(.width(32)) register_4 (.D(DATA_IN), .en(L18), .Q(OUT18), .clk(CLOCK), .clr(RESET));
  Register #(.width(32)) register_5 (.D(DATA_IN), .en(L24), .Q(OUT24), .clk(CLOCK), .clr(RESET));
  Register #(.width(32)) register_6 (.D(DATA_IN), .en(L30), .Q(OUT30), .clk(CLOCK), .clr(RESET));
  Register #(.width(32)) register_7 (.D(DATA_IN), .en(L1), .Q(OUT1), .clk(CLOCK), .clr(RESET));
  Register #(.width(32)) register_8 (.D(DATA_IN), .en(L7), .Q(OUT7), .clk(CLOCK), .clr(RESET));
  Register #(.width(32)) register_9 (.D(DATA_IN), .en(L13), .Q(OUT13), .clk(CLOCK), .clr(RESET));
  Register #(.width(32)) register_10 (.D(DATA_IN), .en(L19), .Q(OUT19), .clk(CLOCK), .clr(RESET));
  Register #(.width(32)) register_11 (.D(DATA_IN), .en(L25), .Q(OUT25), .clk(CLOCK), .clr(RESET));
  Register #(.width(32)) register_12 (.D(DATA_IN_31), .en(ENABLE_31), .Q(STACK_POINTER_OUT), .clk(CLOCK), .clr(RESET));
  Multiplexer #(.select(5), .width(32)) multiplexer_3 (
    .in0(OUT0), .in1(OUT1), .in2(OUT2), .in3(OUT3), .in4(OUT4), .in5(OUT5), .in6(OUT6), .in7(OUT7),
    .in8(OUT8), .in9(OUT9), .in10(OUT10), .in11(OUT11), .in12(OUT12), .in13(OUT13), .in14(OUT14),
    .in15(OUT15), .in16(OUT16), .in17(OUT17), .in18(OUT18), .in19(OUT19), .in20(OUT20), .in21(OUT21),
    .in22(OUT22), .in23(OUT23), .in24(OUT24), .in25(OUT25), .in26(OUT26), .in27(OUT27), .in28(OUT28),
    .in29(OUT29), .in30(OUT30), .in31(STACK_POINTER_OUT), .out(OUT_B), .sel(SELECT_B));  // open: en
  Register #(.width(32)) register_13 (.D(DATA_IN), .en(L2), .Q(OUT2), .clk(CLOCK), .clr(RESET));
  Register #(.width(32)) register_14 (.D(DATA_IN), .en(L8), .Q(OUT8), .clk(CLOCK), .clr(RESET));
  Register #(.width(32)) register_15 (.D(DATA_IN), .en(L14), .Q(OUT14), .clk(CLOCK), .clr(RESET));
  Register #(.width(32)) register_16 (.D(DATA_IN), .en(L20), .Q(OUT20), .clk(CLOCK), .clr(RESET));
  Register #(.width(32)) register_17 (.D(DATA_IN), .en(L26), .Q(OUT26), .clk(CLOCK), .clr(RESET));
  Register #(.width(32)) register_18 (.D(DATA_IN), .en(L3), .Q(OUT3), .clk(CLOCK), .clr(RESET));
  Register #(.width(32)) register_19 (.D(DATA_IN), .en(L9), .Q(OUT9), .clk(CLOCK), .clr(RESET));
  Register #(.width(32)) register_20 (.D(DATA_IN), .en(L15), .Q(OUT15), .clk(CLOCK), .clr(RESET));
  Register #(.width(32)) register_21 (.D(DATA_IN), .en(L21), .Q(OUT21), .clk(CLOCK), .clr(RESET));
  Register #(.width(32)) register_22 (.D(DATA_IN), .en(L27), .Q(OUT27), .clk(CLOCK), .clr(RESET));
  Register #(.width(32)) register_23 (.D(DATA_IN), .en(L4), .Q(OUT4), .clk(CLOCK), .clr(RESET));
  Register #(.width(32)) register_24 (.D(DATA_IN), .en(L10), .Q(OUT10), .clk(CLOCK), .clr(RESET));
  Register #(.width(32)) register_25 (.D(DATA_IN), .en(L16), .Q(OUT16), .clk(CLOCK), .clr(RESET));
  Register #(.width(32)) register_26 (.D(DATA_IN), .en(L22), .Q(OUT22), .clk(CLOCK), .clr(RESET));
  Register #(.width(32)) register_27 (.D(DATA_IN), .en(L28), .Q(OUT28), .clk(CLOCK), .clr(RESET));
  Register #(.width(32)) register_28 (.D(DATA_IN), .en(L5), .Q(OUT5), .clk(CLOCK), .clr(RESET));
  Register #(.width(32)) register_29 (.D(DATA_IN), .en(L11), .Q(OUT11), .clk(CLOCK), .clr(RESET));
  Register #(.width(32)) register_30 (.D(DATA_IN), .en(L17), .Q(OUT17), .clk(CLOCK), .clr(RESET));
  Register #(.width(32)) register_31 (.D(DATA_IN), .en(L23), .Q(OUT23), .clk(CLOCK), .clr(RESET));
  Register #(.width(32)) register_32 (.D(DATA_IN), .en(L29), .Q(OUT29), .clk(CLOCK), .clr(RESET));

  // Other names for the same wires on the sheet: OUT31[31:0] = STACK_POINTER_OUT

  // Notes on the sheet:
  //   INPUTS
  //   OUTPUTS
  //   PLEXERS
  //   REGISTERS
endmodule

module ALU (
  input  [31:0] IN_A,
  input  [31:0] IN_B,
  input  SIGN,
  input  [3:0] OPERATION_SELECTOR,
  output [31:0] OUT,
  output [31:0] LOW,
  output [31:0] HIGH
);

  wire comparator_1_lt, comparator_2_lt, MULT_DIV_SELECTOR, multiplexer_1_out;
  wire [31:0] A_____B, A____B, A____B_t, A___B, A___B_t, A_NOR__B, A_XOR__B, HIGH_PRODUCT, LOW_PRODUCT,
       QUOTIENT, REMAINDER;

  Comparator #(.width(32), .mode("unsigned")) comparator_1 (.a(IN_A), .b(IN_B), .lt(comparator_1_lt));  // open: gt, eq
  Comparator #(.width(32)) comparator_2 (.a(IN_A), .b(IN_B), .lt(comparator_2_lt));  // open: gt, eq
  and and_1 (MULT_DIV_SELECTOR, OPERATION_SELECTOR[0], OPERATION_SELECTOR[1], OPERATION_SELECTOR[2], ~OPERATION_SELECTOR[3]);  // AND_Gate
  Adder #(.width(32)) adder_1 (.a(IN_A), .b(IN_B), .out(A___B));  // open: cin, cout
  Subtractor #(.width(32)) subtractor_1 (.a(IN_A), .b(IN_B), .out(A___B_t));  // open: bin, bout
  assign A____B = IN_A & IN_B;  // AND_Gate and_2, 32 bits wide
  assign A_____B = IN_A | IN_B;  // OR_Gate or_1, 32 bits wide
  assign A_NOR__B = ~(IN_A | IN_B);  // NOR_Gate nor_1, 32 bits wide
  assign A_XOR__B = IN_A ^ IN_B;  // XOR_Gate xor_1, 32 bits wide
  Multiplier #(.width(32)) multiplier_1 (.a(IN_A), .b(IN_B), .out(LOW_PRODUCT), .cout(HIGH_PRODUCT));  // open: cin
  Divider #(.width(32)) divider_1 (.a(IN_A), .b(IN_B), .out(QUOTIENT), .rem(REMAINDER));  // open: upper
  Multiplexer multiplexer_1 (
    .in0(comparator_1_lt), .in1(comparator_2_lt), .out(multiplexer_1_out), .sel(SIGN));  // open: en
  assign A____B_t = {{31{1'b0}}, multiplexer_1_out};  // Bit_Extender bit_extender_1
  Multiplexer #(.select(4), .width(32)) multiplexer_2 (
    .in0(A___B), .in1(A___B_t), .in2(A____B), .in3(A_____B), .in4(A_NOR__B), .in5(A_XOR__B), .in6(A____B_t),
    .out(OUT), .sel(OPERATION_SELECTOR));  // open: in7, in8, in9, in10, in11, in12, in13, in14, in15, en
  Multiplexer #(.width(32)) multiplexer_3 (
    .in0(QUOTIENT), .in1(LOW_PRODUCT), .out(LOW), .sel(MULT_DIV_SELECTOR));  // open: en
  Multiplexer #(.width(32)) multiplexer_4 (
    .in0(REMAINDER), .in1(HIGH_PRODUCT), .out(HIGH), .sel(MULT_DIV_SELECTOR));  // open: en
  // AND_Gate and_3 is placed but not wired

  // Notes on the sheet:
  //   INPUTS
  //   OUTPUTS
endmodule

module ALU_Manager (
  input  SUB,
  input  NOR,
  input  MULT,
  input  MULU,
  input  DIV,
  input  DIVU,
  input  AND,
  input  ANDI,
  input  OR,
  input  ORI,
  input  XOR,
  input  XORI,
  input  SLT,
  input  SLTU,
  input  SLTI,
  input  SLTIU,
  output [3:0] ALU_SELECTOR,
  output ALU_SIGN
);

  wire AND_OP, MULT_OP, OR_OP, SLT_OP, UNSIGNED, XOR_OP;

  or or_1 (MULT_OP, MULT, MULU);
  or or_2 (ALU_SELECTOR[3], DIV, DIVU);
  or or_3 (AND_OP, AND, ANDI);
  or or_4 (OR_OP, OR, ORI);
  or or_5 (XOR_OP, XOR, XORI);
  or or_6 (SLT_OP, SLT, SLTU, SLTI, SLTIU);
  or or_7 (UNSIGNED, SLTU, SLTIU, MULU, DIVU);
  and and_1 (ALU_SIGN, ~UNSIGNED, 1'b1);  // AND_Gate
  or or_8 (ALU_SELECTOR[0], SUB, OR_OP, NOR, MULT_OP);
  or or_9 (ALU_SELECTOR[1], AND_OP, OR_OP, SLT_OP, MULT_OP);
  or or_10 (ALU_SELECTOR[2], XOR_OP, NOR, SLT_OP, MULT_OP);

  // Other names for the same wires on the sheet: DIV_OP = ALU_SELECTOR[3]

  // Notes on the sheet:
  //   INPUTS
endmodule

module Instruction_RAM_Data_Registers (
  input  [31:0] DATA_IN,
  input  ENABLE_RAM_DATA,
  input  ENABLE_INSTRUCTION,
  input  CLOCK,
  input  RESET,
  output [31:0] INSTRUCTION_REGISTER,
  output [31:0] RAM_DATA_REGISTER
);

  Register #(.width(32)) register_1 (
    .D(DATA_IN), .en(ENABLE_INSTRUCTION), .Q(INSTRUCTION_REGISTER), .clk(CLOCK), .clr(RESET));
  Register #(.width(32)) register_2 (
    .D(DATA_IN), .en(ENABLE_RAM_DATA), .Q(RAM_DATA_REGISTER), .clk(CLOCK), .clr(RESET));

  // Notes on the sheet:
  //   INPUTS
  //   OUTPUTS
endmodule

module Low_High_Registers (
  input  [31:0] IN_LOW,
  input  [31:0] IN_HIGH,
  input  ENABLE,
  input  CLOCK,
  input  RESET,
  output [31:0] OUT_LOW,
  output [31:0] OUT_HIGH
);

  Register #(.width(32)) register_1 (.D(IN_LOW), .en(ENABLE), .Q(OUT_LOW), .clk(CLOCK), .clr(RESET));
  Register #(.width(32)) register_2 (.D(IN_HIGH), .en(ENABLE), .Q(OUT_HIGH), .clk(CLOCK), .clr(RESET));

  // Notes on the sheet:
  //   INPUTS
  //   OUTPUTS
endmodule

module PC_Register (
  input  [31:0] IN_PC,
  input  ENABLE_PC,
  input  CLOCK,
  input  RESET,
  output [31:0] OUT_PC
);

  Register #(.width(32)) register_1 (.D(IN_PC), .en(ENABLE_PC), .Q(OUT_PC), .clk(CLOCK), .clr(RESET));
endmodule

module Timer (
  input  START,
  input  [3:0] TIME,
  input  CLOCK,
  input  RESET,
  output TIME_OUT
);

  wire [3:0] counter_1_q;

  Counter #(.width(4), .max('hf)) counter_1 (
    .count(START), .Q(counter_1_q), .clk(CLOCK), .clr(RESET));  // open: load, D, carry
  Comparator #(.width(4)) comparator_1 (.a(TIME), .b(counter_1_q), .eq(TIME_OUT));  // open: gt, lt
endmodule

module _4_Byte_Flipper (
  input  [31:0] IN,
  output [31:0] OUT
);


  assign OUT = {IN[7:0], IN[15:8], IN[23:16], IN[31:24]};
endmodule
